# Fritzing sketch Circuit (saved by Fritzing 0.9.3b)

parts:
  Part1 = Arduino Uno (Rev3)
  A1 = BBAA100043

nets:
  N1: Part1.D11_PWM/MOSI, A1.pin1
  N2: Part1.D12/MISO, A1.pin2
  N3: Part1.D13/SCK, A1.pin3
  N4: Part1.GND, A1.pin4

custom parts:
  BBAA100043: BBAA100043 traffic light module.
